# Fritzing sketch circuit_diagram (saved by Fritzing 0.9.3b)
breadboards: 2

parts:
  74HCT688E1 = IC, DIP package, 20 pins [chip_label=74HCT688E]
  74HCT688E2 = IC, DIP package, 20 pins [chip_label=74HCT688E]
  74HCT688E3 = IC, DIP package, 20 pins [chip_label=74HCT688E]
  74HCT688E4 = IC, DIP package, 20 pins [chip_label=74HCT688E]
  74HCT688E6 = IC, DIP package, 14 pins [chip_label=74HCT32N]
  74HCT688E7 = IC, DIP package, 14 pins [chip_label=74HCT125N]
  74HCT688E8 = IC, DIP package, 16 pins [chip_label=74HC595N]
  74HCT688E9 = IC, DIP package, 14 pins [chip_label=74HCT32N]
  Part1 = Logic Level Converter
  Part2 = Logic Level Converter

nets:
  N1: 74HCT688E1.pin2, 74HCT688E1.pin6, 74HCT688E2.pin6, 74HCT688E3.pin4, 74HCT688E3.pin6, 74HCT688E4.pin2, 74HCT688E4.pin4, 74HCT688E4.pin6
  N2: 74HCT688E1.pin4, 74HCT688E1.pin8, 74HCT688E1.pin10, 74HCT688E2.pin2, 74HCT688E2.pin4, 74HCT688E2.pin8, 74HCT688E2.pin10, 74HCT688E3.pin2, 74HCT688E3.pin8, 74HCT688E3.pin10, 74HCT688E4.pin8, 74HCT688E4.pin10, 74HCT688E6.pin7
  N3: 74HCT688E1.pin11, 74HCT688E2.pin11, 74HCT688E3.pin11, 74HCT688E4.pin11
  N4: 74HCT688E1.pin12, 74HCT688E1.pin14, 74HCT688E1.pin16, 74HCT688E1.pin18, 74HCT688E1.pin20, 74HCT688E2.pin12, 74HCT688E2.pin14, 74HCT688E2.pin16, 74HCT688E2.pin18, 74HCT688E2.pin20, 74HCT688E3.pin12, 74HCT688E3.pin14, 74HCT688E3.pin16, 74HCT688E3.pin18, 74HCT688E3.pin20, 74HCT688E4.pin12, 74HCT688E4.pin14, 74HCT688E4.pin16, 74HCT688E4.pin18, 74HCT688E4.pin20, 74HCT688E6.pin14, Part1.HV
  N5: 74HCT688E1.pin13, 74HCT688E2.pin13, 74HCT688E3.pin13, 74HCT688E4.pin13
  N6: 74HCT688E1.pin15, 74HCT688E2.pin15, 74HCT688E3.pin15, 74HCT688E4.pin15
  N7: 74HCT688E1.pin17, 74HCT688E2.pin17, 74HCT688E3.pin17, 74HCT688E4.pin17
  N8: 74HCT688E1.pin19, 74HCT688E6.pin10
  N9: 74HCT688E2.pin19, 74HCT688E6.pin13
  N10: 74HCT688E3.pin19, 74HCT688E6.pin1
  N11: 74HCT688E4.pin19, 74HCT688E6.pin4
  N12: 74HCT688E6.pin2, 74HCT688E6.pin5, 74HCT688E6.pin9, 74HCT688E6.pin12, 74HCT688E9.pin1, 74HCT688E9.pin4, Part1.TX_HV
  N13: 74HCT688E6.pin3, Part1.GND
  N14: 74HCT688E6.pin6, Part1.TX2_HV
  N15: 74HCT688E6.pin8, Part1.RX_HV
  N16: 74HCT688E7.pin1, 74HCT688E7.pin7, 74HCT688E8.pin8, 74HCT688E9.pin7
  N17: 74HCT688E7.pin14, 74HCT688E8.pin10, 74HCT688E8.pin16, 74HCT688E9.pin14, Part2.HV
  N18: 74HCT688E8.pin13, 74HCT688E9.pin6
  N19: 74HCT688E9.pin3, Part2.RX_HV

notes:
  Raspberry Pi #2
  +3.3V
  GND
  8
  10
  6
  16
  Raspberry Pi
  #1
  +3.3V
  GND
  16
  10
  8
  12
  22
  GND
  +5V
  Vectron 64 Address Bus
  15 14 13 12 11 10 9 8
  Vectron 64 Address Bus
  0 1 2 3 4 5 6 7
  6502 Interrupt
  Vectron 64 Data Bus
  0
  1
  2
  3
  4
  5
  6
  7
  FFF9 on Vectron 64
  Address Bus (L == true)
  FFF8 on Vectron 64
  Address Bus (L == true)
  FFFF on Vectron 64
  Address Bus (L == true)
